// Logisim project Divider CRC Circuit.circ as structural Verilog: 1 circuit, main circuit main
module main (
  input  in_1
);

  wire clock_1_out, j_k_ff_1_q, j_k_ff_2_q, j_k_ff_3_q, j_k_ff_4_q, not_1_out, not_2_out, not_3_out,
       not_4_out, xor_1_out, xor_2_out;

  Clock clock_1 (.out(clock_1_out));
  xor xor_1 (xor_1_out, j_k_ff_4_q, in_1);
  not not_1 (not_1_out, xor_1_out);
  J_K_Flip_Flop #(.trigger("falling")) j_k_ff_1 (
    .J(xor_1_out), .clk(clock_1_out), .K(not_1_out), .Q(j_k_ff_1_q));  // open: Qn, preset, en, reset
  // Probe on j_k_ff_1_q
  not not_2 (not_2_out, j_k_ff_1_q);
  J_K_Flip_Flop #(.trigger("falling")) j_k_ff_2 (
    .J(j_k_ff_1_q), .clk(clock_1_out), .K(not_2_out), .Q(j_k_ff_2_q));  // open: Qn, preset, en, reset
  // Probe on j_k_ff_2_q
  J_K_Flip_Flop #(.trigger("falling")) j_k_ff_3 (
    .J(j_k_ff_2_q), .clk(clock_1_out), .K(not_3_out), .Q(j_k_ff_3_q));  // open: Qn, preset, en, reset
  not not_3 (not_3_out, j_k_ff_2_q);
  // Probe on j_k_ff_3_q
  xor xor_2 (xor_2_out, j_k_ff_4_q, j_k_ff_3_q);
  J_K_Flip_Flop #(.trigger("falling")) j_k_ff_4 (
    .J(xor_2_out), .clk(clock_1_out), .K(not_4_out), .Q(j_k_ff_4_q));  // open: Qn, preset, en, reset
  not not_4 (not_4_out, xor_2_out);
  // Probe on j_k_ff_4_q

  // Notes on the sheet:
  //   in_1: pull=down
endmodule
